# Fritzing sketch IR-Receiver (saved by Fritzing 0.9.2b)

parts:
  Raspberry_Pi1 = Raspberry Pi B+
  Part1 = IR Receiver Breakout [package=PCB]

nets:
  3V3: Raspberry_Pi1.3v3, Part1.VCC
  GND: Raspberry_Pi1.GND, Part1.GND
  N1: Raspberry_Pi1.GPIO18, Part1.IN

notes:
  This is small breakout board that the IR LED plugs into. The colors are those of the included wires

custom parts:
  IR Receiver Breakout: Sensor uses HX1838, high sensitivity Operating voltage 5V Digital output VCC external 3.3V-5V voltage (can be directly connected with the a 5v microcontroller and 3.3v microcontroller) GND external GND IN an external microcontroller I / O port, I / O port has been designed 10K pull-up resistor
