# Fritzing sketch CallButton (saved by Fritzing 0.9.3b)
breadboards: 1

parts:
  Part1 = Arduino Pro Mini (5V)
  Part2 = NRF24L01+ Breakout Board
  C1 = Capacitor [package=cap-pth-small2]
  R1 = Resistor [tolerance=±5% resistance=82 package="0603 [SMD]"]
  D1 = Zener Diode [part_number=1N4732A breakdown_voltage=3.3V package="300 mil [THT]"]
  LED1 = LED - 3mm [color="Green (565nm)" package="3 mm [THT]"]
  LED2 = LED - 3mm [color="Red (635nm)" package="3 mm [THT]"]
  S1 = Pushbutton [package="[THT]"]
  C2 = Capacitor [package=cap-pth-small2]
  R2 = Resistor [tolerance=±5% resistance=330k package="0603 [SMD]"]
  R3 = Resistor [tolerance=±5% resistance=330k package="0603 [SMD]"]

nets:
  GND: Part1.GND, Part2.GND, C1.1, D1.anode, LED1.cathode, LED2.anode, S1.Pin_1, S1.Pin_2, C2.2
  N1: Part1.VCC, R1.Pin_1
  N2: Part1.MISO, Part2.SCK
  N3: Part1.MOSI, Part2.MISO
  N4: Part1.D10, Part2.MOSI
  N5: Part1.D9, R2.Pin_1
  N6: Part1.D8, Part2.CS
  N7: Part1.D7, Part2.CE
  N8: Part1.D6, R3.Pin_1
  N9: Part1.D5, S1.Pin_3, S1.Pin_4, C2.1
  N10: Part2.VCC, C1.2, R1.Pin_0, D1.cathode
  N11: LED1.anode, R2.Pin_0
  N12: LED2.cathode, R3.Pin_0

notes:
  3.3V Zener + 82Ohm resistor for simple regulator for NRF245L01
  330 Ohm resistors for LEDs and .1uF capictors for power/bounce smoothing
  This is the Caller. The receiver is the same but only one LED and no button
