# Fritzing sketch NeopixelBacklight (saved by Fritzing 0.9.2b)
breadboards: 1

parts:
  Part5 = Arduino Pro Mini v13
  U1 = POT [package=pot_mammoth]
  U2 = POT [package=pot_mammoth]
  neopixel1 = Neopixel Ring 12
  C4 = Electrolytic Capacitor [capacitance=1000μF package="1010 [SMD, electrolytic]"]

nets:
  GND: Part5.GND, U1.S, U2.E, neopixel1.GND, C4.+
  VCC: Part5.VCC, U1.E, U2.S, neopixel1.VCC, C4.-
  N1: Part5.A1, U2.A
  N2: Part5.A0, U1.A
  N3: Part5.D6_PWM, neopixel1.IN

notes:
  Color selection
  Brightness selection
  Neopixel ring with
  color and brightness controlled via pots

custom parts:
  Neopixel Ring 12: Neopixel Ring x12

// code stored in the sketch: NeopixelBacklight.ino
#include <Adafruit_NeoPixel.h>
#ifdef __AVR__
  #include <avr/power.h>
#endif

#define NEOPIXEL_DATA_PIN 6
#define NEOPIXEL_LEDS 12
#define ANALOG_COLOR_PIN A0  
#define ANALOG_BRIGHTNESS_PIN A1  
#define SWIPE_WAIT 50

// Parameter 1 = number of pixels in strip
// Parameter 2 = Arduino pin number (most are valid)
// Parameter 3 = pixel type flags, add together as needed:
//   NEO_KHZ800  800 KHz bitstream (most NeoPixel products w/WS2812 LEDs)
//   NEO_KHZ400  400 KHz (classic 'v1' (not v2) FLORA pixels, WS2811 drivers)
//   NEO_GRB     Pixels are wired for GRB bitstream (most NeoPixel products)
//   NEO_RGB     Pixels are wired for RGB bitstream (v1 FLORA pixels, not v2)
Adafruit_NeoPixel strip = Adafruit_NeoPixel(NEOPIXEL_LEDS, NEOPIXEL_DATA_PIN, NEO_GRB + NEO_KHZ800);

// IMPORTANT: To reduce NeoPixel burnout risk, add 1000 uF capacitor across
// pixel power leads, add 300 - 500 Ohm resistor on first pixel's data input
// and minimize distance between Arduino and first pixel.  Avoid connecting
// on a live circuit...if you must, connect GND first.

byte sensorValue = 0;        // value read from the pot
float brightnessValue = 1.0;   // value read from the pot

void setup() {
  // This is for Trinket 5V 16MHz, you can remove these three lines if you are not using a Trinket
  #if defined (__AVR_ATtiny85__)
    if (F_CPU == 16000000) clock_prescale_set(clock_div_1);
  #endif
  // End of trinket special code


  strip.begin();
  strip.show(); // Initialize all pixels to 'off'

  Serial.begin(9600);
  while (!Serial) {
    ; // wait for serial port to connect. Needed for native USB port only
  }  
}

void loop() 
{

  // read the analog in value:
  byte newSensorValue = map(analogRead(ANALOG_COLOR_PIN), 0, 1023, 0, 255);
  bool updateNeo = false;
  if ( newSensorValue != sensorValue )
  {
      sensorValue = newSensorValue;
      updateNeo = true;
  }
  float newSensorBrightness = map(analogRead(ANALOG_BRIGHTNESS_PIN), 0, 1023, 0, 255);
  
  if (  brightnessValue != newSensorBrightness )
  {
      updateNeo = true;
      brightnessValue = newSensorBrightness;
      strip.setBrightness(brightnessValue);
  }
  
  if ( updateNeo )
  {
    colorWipe(Wheel(sensorValue),SWIPE_WAIT);
  }

}

// Fill the dots one after the other with a color
void colorWipe(uint32_t c, uint8_t wait) {
  for(uint16_t i=0; i<strip.numPixels(); i++) {
    strip.setPixelColor(i, c);
    strip.show();
    delay(wait);
  }
}

void rainbow(uint8_t wait) {
  uint16_t i, j;

  for(j=0; j<256; j++) {
    for(i=0; i<strip.numPixels(); i++) {
      strip.setPixelColor(i, Wheel((i+j) & 255));
    }
    strip.show();
    delay(wait);
  }
}

// Slightly different, this makes the rainbow equally distributed throughout
void rainbowCycle(uint8_t wait) {
  uint16_t i, j;

  for(j=0; j<256*5; j++) { // 5 cycles of all colors on wheel
    for(i=0; i< strip.numPixels(); i++) {
      strip.setPixelColor(i, Wheel(((i * 256 / strip.numPixels()) + j) & 255));
    }
    strip.show();
    delay(wait);
  }
}

//Theatre-style crawling lights.
void theaterChase(uint32_t c, uint8_t wait) {
  for (int j=0; j<10; j++) {  //do 10 cycles of chasing
    for (int q=0; q < 3; q++) {
      for (int i=0; i < strip.numPixels(); i=i+3) {
        strip.setPixelColor(i+q, c);    //turn every third pixel on
      }
      strip.show();

      delay(wait);

      for (int i=0; i < strip.numPixels(); i=i+3) {
        strip.setPixelColor(i+q, 0);        //turn every third pixel off
      }
    }
  }
}

//Theatre-style crawling lights with rainbow effect
void theaterChaseRainbow(uint8_t wait) {
  for (int j=0; j < 256; j++) {     // cycle all 256 colors in the wheel
    for (int q=0; q < 3; q++) {
      for (int i=0; i < strip.numPixels(); i=i+3) {
        strip.setPixelColor(i+q, Wheel( (i+j) % 255));    //turn every third pixel on
      }
      strip.show();

      delay(wait);

      for (int i=0; i < strip.numPixels(); i=i+3) {
        strip.setPixelColor(i+q, 0);        //turn every third pixel off
      }
    }
  }
}

// Input a value 0 to 255 to get a color value.
// The colours are a transition r - g - b - back to r.
uint32_t Wheel(byte WheelPos) {
  WheelPos = 255 - WheelPos;
  if(WheelPos < 85) {
    return strip.Color(255 - WheelPos * 3, 0, WheelPos * 3);
  }
  if(WheelPos < 170) {
    WheelPos -= 85;
    return strip.Color(0, WheelPos * 3, 255 - WheelPos * 3);
  }
  WheelPos -= 170;
  return strip.Color(WheelPos * 3, 255 - WheelPos * 3, 0);
}
