# Fritzing sketch NeoPixelNightLight-Huzzah (saved by Fritzing 0.9.3b)
breadboards: 1

parts:
  U2 = POT [package=pot_mammoth]
  S1 = Momentary Switch [package=ksa_sealed_tac_switch]
  neopixel2 = Neopixel Ring 12
  C5 = Electrolytic Capacitor [capacitance=1000μF package="1010 [SMD, electrolytic]"]
  Adafruit_HUZZAH_ESP8266_Breakout1 = Adafruit HUZZAH ESP8266 Breakout [part_number=2471]
  R1 = Resistor [tolerance=±5% resistance=1k package="0603 [SMD]"]
  R2 = Resistor [tolerance=±5% resistance=220 package="0603 [SMD]"]

nets:
  N1: U2.S, R1.Pin_1, R2.Pin_0
  N2: U2.A, Adafruit_HUZZAH_ESP8266_Breakout1.A
  GND: U2.E, neopixel2.GND, C5.-, Adafruit_HUZZAH_ESP8266_Breakout1.GND, R2.Pin_1
  N3: S1.1, S1.3, neopixel2.VCC, Adafruit_HUZZAH_ESP8266_Breakout1.V+, R1.Pin_0
  N4: S1.2, S1.4, Adafruit_HUZZAH_ESP8266_Breakout1.#13
  N5: neopixel2.IN, Adafruit_HUZZAH_ESP8266_Breakout1.#14

notes:
  Brightness and color selection
  Mode
  button
  5V External power
  1v voltage divider since analog only takes 1v

custom parts:
  Neopixel Ring 12: Neopixel Ring x12
