# Fritzing sketch NeoPixelNightLight (saved by Fritzing 0.9.2b)
breadboards: 1

parts:
  Part1 = Arduino Pro Mini v13
  U2 = POT [package=pot_mammoth]
  U3 = POT [package=pot_mammoth]
  S1 = Momentary Switch [package=ksa_sealed_tac_switch]
  S2 = Toggle Switch [package=THT]
  neopixel2 = Neopixel Ring 12
  C5 = Electrolytic Capacitor [capacitance=1000μF package="1010 [SMD, electrolytic]"]
  VCC1 = 4 x AAA Battery Mount
  RTC1 = DS1307 RTC Breakout

nets:
  VCC: Part1.VCC, U2.S, U3.E, S1.1, S1.3, S2.L1, neopixel2.VCC, RTC1.5V
  GND: Part1.GND, U2.E, U3.S, neopixel2.GND, C5.-, VCC1.-, RTC1.GND
  N1: Part1.A3, RTC1.SDA
  N2: Part1.A2, RTC1.SCL
  N3: Part1.A1, U2.A
  N4: Part1.A0, U3.A
  N5: Part1.D10_PWM/SS, S1.2, S1.4
  N6: Part1.D6_PWM, neopixel2.IN
  N7: S2.COM, VCC1.+

notes:
  Color selection
  Brightness selection
  On/off
  Mode
  5V External power

custom parts:
  Neopixel Ring 12: Neopixel Ring x12
  DS1307 RTC Breakout: DS1307 Real-time Clock Breakout Board with Battery
