# Fritzing sketch BasicHC-SR04Ultrasonic (saved by Fritzing 0.9.2b)
breadboards: 1

parts:
  Raspberry_Pi1 = Raspberry Pi 2
  U1 = HC-SR04 [chip_label=IC package="SIP (Single Inline) [THT]"]
  R1 = Resistor [tolerance=±5% resistance=330 package=THT]
  R2 = Resistor [tolerance=±5% resistance=220 package=THT]

nets:
  N1: Raspberry_Pi1.GPIO13, U1.Trig
  N2: Raspberry_Pi1.GPIO19, Raspberry_Pi1.GPIO26, R1.Pin_1, R2.Pin_0
  GND: Raspberry_Pi1.GPIO14, Raspberry_Pi1.GND, U1.GND, R2.Pin_1
  5V: Raspberry_Pi1.5V, U1.Vcc
  N3: U1.Echo, R1.Pin_0

notes:
  http://www.raspberrypi-spy.co.uk/2012/12/ultrasonic-distance-measurement-using-python-part-1/
  Since Pi can't take 5v on echo input, use two restistors to drop voltage. See web link for details, but R1> R2, and ideally R1 == 2*R2 to drop 5v to 2/3 or 3.33v

custom parts:
  HC-SR04: HC-SR04 ultrasound distance sensor
