# Fritzing sketch CarHatchDetector (saved by Fritzing 0.9.2b)
breadboards: 1

parts:
  K1 = Relay [part_number=FRS1B-S package=THT]
  Q1 = NPN-Transistor [package="TO92 [THT]"]
  R1 = Resistor [tolerance=±5% resistance=1k package=THT]
  D1 = Rectifier Diode [part_number=1N4001 package="300 mil [THT]"]
  Part2 = Arduino Pro Mini v13
  U2 = HC-SR04 [chip_label=IC package="SIP (Single Inline) [THT]"]
  J1 = Piezo Speaker

nets:
  N1: K1.COIL1, Q1.C, D1.anode
  VCC: K1.COIL2, Part2.VCC, U2.Vcc
  GND: Q1.E, Part2.GND, U2.GND, J1.pin1
  N2: Q1.B, R1.Pin_1
  N3: R1.Pin_0, Part2.D8
  N4: Part2.D7, U2.Trig
  N5: Part2.D6_PWM, U2.Echo
  N6: Part2.D3_PWM, J1.pin2

notes:
  Connect door saftey to NC leads of relay.
  Relay circuit from Sunfounder example

custom parts:
  HC-SR04: HC-SR04 ultrasound distance sensor
