# Fritzing sketch HC-SR04UltrasonicWithLED (saved by Fritzing 0.9.2b)
breadboards: 1

parts:
  Raspberry_Pi1 = Raspberry Pi 2
  UltrasonicSensor = HC-SR04 [chip_label=IC package="SIP (Single Inline) [THT]"]
  R1 = Resistor [tolerance=±5% resistance=330 package=THT]
  R2 = Resistor [tolerance=±5% resistance=220 package=THT]
  LEDBlue = LED - 5mm [color="Blue (430nm)" package="5 mm [THT]"]
  LEDGreen = LED - 5mm [color="Green (555nm)" package="5 mm [THT]"]
  LEDRed = LED - 5mm [color="Red (633nm)" package="5 mm [THT]"]
  R3 = Resistor [tolerance=±5% resistance=220 package=THT]
  R7 = Resistor [tolerance=±5% resistance=220 package=THT]
  R8 = Resistor [tolerance=±5% resistance=220 package=THT]
  Passive = Piezo Speaker [part_number=passive]
  Q1 = TRANSISTOR_PNP [part_number=8550 package=to-92]
  R9 = Resistor [tolerance=±5% resistance=1k package=THT]

nets:
  GND: Raspberry_Pi1.GND, UltrasonicSensor.GND, R2.Pin_1, LEDBlue.anode, LEDGreen.anode, LEDRed.anode, Q1.C
  N1: Raspberry_Pi1.GPIO5, UltrasonicSensor.Trig
  N2: Raspberry_Pi1.GPIO6, R1.Pin_1, R2.Pin_0
  N3: Raspberry_Pi1.GPIO13, R3.Pin_0
  N4: Raspberry_Pi1.GPIO19, R7.Pin_0
  N5: Raspberry_Pi1.GPIO26, R8.Pin_0
  N6: Raspberry_Pi1.GPIO16, R9.Pin_0
  5V: Raspberry_Pi1.5V, UltrasonicSensor.Vcc, Passive.pin2
  N7: UltrasonicSensor.Echo, R1.Pin_0
  N8: LEDBlue.cathode, R3.Pin_1
  N9: LEDGreen.cathode, R7.Pin_1
  N10: LEDRed.cathode, R8.Pin_1
  N11: Passive.pin1, Q1.E
  N12: Q1.B, R9.Pin_1

notes:
  http://www.raspberrypi-spy.co.uk/2012/12/ultrasonic-distance-measurement-using-python-part-1/
  Since Pi can't take 5v on echo input, use two restistors to drop voltage. See web link for details, but R1> R2, and ideally R1 == 2*R2 to drop 5v to 2/3 or 3.33v

custom parts:
  HC-SR04: HC-SR04 ultrasound distance sensor
